# Fritzing sketch 12F1822-Curcuit (saved by Fritzing 0.9.3b)
breadboards: 1

parts:
  Raspberry_Pi_1 = Raspberry Pi 3 [part_number=RPI-3-V1.2]
  12F1822 = PICAXE-08M [package=THT]
  R1 = Rotary Potentiometer (Small) [maximum_resistance=100kΩ package=THT]
  R2 = Rotary Potentiometer (Small) [maximum_resistance=100kΩ package=THT]

nets:
  3V3: Raspberry_Pi_1.3v3, Raspberry_Pi_1.3V3, 12F1822.+V, R1.leg1, R2.leg1
  N1: Raspberry_Pi_1.GPIO2, 12F1822.In/Out_1_/_ADC_1
  N2: Raspberry_Pi_1.GPIO3, 12F1822.In/Out_2_/_ADC_2_/_PWM_2
  N3: Raspberry_Pi_1.GND, 12F1822.0V, R1.leg2, R2.leg2
  N4: 12F1822.In/Out_4_/_ADC_4, R2.wiper
  N5: 12F1822.Serial_Out_/_Out_0_/_Infraout, R1.wiper
